// Logisim project И-НЕ.circ as structural Verilog: 1 circuit, main circuit И-НЕ
module \И_НЕ  (
  input  A,
  input  B,
  output Y
);

  wire transistor_3_out;

  Transistor #(.\type ("p")) transistor_1 (.in(1'b1), .out(Y), .gate(B));
  Transistor #(.\type ("n")) transistor_2 (.in(transistor_3_out), .out(Y), .gate(B));
  Transistor #(.\type ("n")) transistor_3 (.in(1'b0), .out(transistor_3_out), .gate(A));
  Transistor #(.\type ("p")) transistor_4 (.in(1'b1), .out(Y), .gate(A));

  // Notes on the sheet:
  //   VT2
  //   VT4
  //   VT3
  //   VT1
endmodule
