// Logisim project МКНФ.circ as structural Verilog: 1 circuit, main circuit МКНФ
module \МКНФ  (
  input  a,
  input  b,
  input  c,
  input  d,
  output F
);

  wire not_1_out, not_2_out, not_3_out, not_4_out, or_1_out, or_2_out, or_3_out, or_4_out, undriven,
       undriven_2, undriven_3, undriven_4, undriven_5, undriven_6, undriven_7, undriven_8, undriven_9,
       undriven_10, undriven_11, undriven_12, undriven_13;

  not not_1 (not_1_out, a);
  not not_2 (not_2_out, b);
  not not_3 (not_3_out, c);
  not not_4 (not_4_out, d);
  or or_1 (or_1_out, undriven_4, undriven_8, undriven_12);
  or or_2 (or_2_out, undriven, undriven_5, undriven_9, undriven_11);
  or or_3 (or_3_out, undriven_2, undriven_6, undriven_13);
  or or_4 (or_4_out, undriven_3, undriven_7, undriven_10);
  and and_1 (F, or_1_out, or_2_out, or_3_out, or_4_out);
endmodule
