// Logisim project СДНФ.circ as structural Verilog: 1 circuit, main circuit СДНФ
module \СДНФ  (
  input  a,
  input  b,
  input  c,
  input  d,
  output F
);

  wire and_1_out, and_2_out, and_3_out, and_4_out, and_5_out, and_6_out, and_7_out, and_8_out, and_9_out,
       not_1_out, not_2_out, not_3_out, not_4_out, undriven, undriven_2, undriven_3, undriven_4, undriven_5,
       undriven_6, undriven_7, undriven_8, undriven_9, undriven_10, undriven_11, undriven_12, undriven_13,
       undriven_14, undriven_15, undriven_16, undriven_17, undriven_18, undriven_19, undriven_20,
       undriven_21, undriven_22, undriven_23, undriven_24, undriven_25, undriven_26, undriven_27,
       undriven_28, undriven_29, undriven_30, undriven_31, undriven_32, undriven_33, undriven_34,
       undriven_35, undriven_36;

  not not_1 (not_1_out, a);
  not not_2 (not_2_out, b);
  not not_3 (not_3_out, c);
  not not_4 (not_4_out, d);
  and and_1 (and_1_out, undriven_6, undriven_14, undriven_23, undriven_31);
  and and_2 (and_2_out, undriven_7, undriven_15, undriven_19, undriven_28);
  and and_3 (and_3_out, undriven_8, undriven_10, undriven_24, undriven_32);
  and and_4 (and_4_out, undriven_9, undriven_11, undriven_20, undriven_33);
  and and_5 (and_5_out, undriven, undriven_16, undriven_25, undriven_34);
  and and_6 (and_6_out, undriven_2, undriven_17, undriven_21, undriven_35);
  and and_7 (and_7_out, undriven_3, undriven_18, undriven_22, undriven_29);
  and and_8 (and_8_out, undriven_4, undriven_12, undriven_26, undriven_36);
  and and_9 (and_9_out, undriven_5, undriven_13, undriven_27, undriven_30);
  or or_1 (F, and_1_out, and_2_out, and_3_out, and_4_out, and_5_out, and_6_out, and_7_out, and_8_out, and_9_out);
endmodule
