// Logisim project JK-триггер.circ as structural Verilog: 1 circuit, main circuit JK-триггер, внутреннее устройство
module \JK_триггер__внутреннее_устройство  (
  input  J,
  input  K,
  input  C,
  output Q,
  output nQ
);

  wire and_1_out, and_2_out, not_1_out, or_1_out, undriven, undriven_2;

  not not_1 (not_1_out, K);
  and and_1 (and_1_out, J, undriven_2);
  and and_2 (and_2_out, not_1_out, undriven);
  or or_1 (or_1_out, and_1_out, and_2_out);
  D_Flip_Flop d_ff_1 (.clk(or_1_out), .D(C), .Q(Q), .Qn(nQ));  // open: preset, en, reset

  // Notes on the sheet:
  //   не K
  //   C - такт, по переднему фронту записывается D
  //   JK-триггер: D-триггер + логика D = J·(не Q) или (не K)·Q
  //   J и не Q
  //   не K и Q
  //   ИЛИ
  //   D-триггер
endmodule
