// Logisim project Демультиплексор.circ as structural Verilog: 1 circuit, main circuit Демультиплексор 1-4
module \Демультиплексор_1_4  (
  input  I,
  input  a1,
  input  a0,
  output F0,
  output F1,
  output F2,
  output F3
);

  wire not_1_out, not_2_out, not_3_out, undriven, undriven_2, undriven_3, undriven_4, undriven_5, undriven_6,
       undriven_7, undriven_8, undriven_9, undriven_10, undriven_11, undriven_12;

  not not_1 (not_1_out, I);
  not not_2 (not_2_out, a1);
  not not_3 (not_3_out, a0);
  and and_1 (F0, undriven, undriven_7, undriven_11);
  and and_2 (F1, undriven_2, undriven_8, undriven_9);
  and and_3 (F2, undriven_3, undriven_5, undriven_12);
  and and_4 (F3, undriven_4, undriven_6, undriven_10);

  // Notes on the sheet:
  //   Демультиплексор 1-4: I - информационный вход, a1 a0 - адресные входы
endmodule
