// Logisim project Счетчик.circ as structural Verilog: 1 circuit, main circuit Счетчик, вариант 11
module \Счетчик__вариант_11  (
  input  a,
  input  b
);

  wire clk, n0, n1, n2, n3, na, nb, not_1_out, not_4_out, not_5_out, not_6_out, q0, q1, q2, q3, r1, r2, r3,
       r4, r5, r6, s0, s1, s2, s3, s4, s5, s6, s7, s8, s9, s10, s11, s12, s13, s14, s15, undriven,
       undriven_2, undriven_3, undriven_4, undriven_5, undriven_6, undriven_7, undriven_8, undriven_9,
       undriven_10, undriven_11, undriven_12, undriven_13, undriven_14, undriven_15, undriven_16,
       undriven_17, undriven_18, undriven_19, undriven_20, undriven_21, undriven_22, undriven_23,
       undriven_24, undriven_25, undriven_26, undriven_27, undriven_28, undriven_29, undriven_30,
       undriven_31, undriven_32, undriven_33, undriven_34, undriven_35, undriven_36, undriven_37,
       undriven_38, undriven_39, undriven_40, undriven_41, undriven_42, undriven_43, undriven_44,
       undriven_45, undriven_46, undriven_47, undriven_48, undriven_49, undriven_50, undriven_51,
       undriven_52, undriven_53, undriven_54, undriven_55, undriven_56, undriven_57, undriven_58,
       undriven_59, undriven_60, undriven_61, undriven_62, undriven_63, undriven_64;
  wire [3:1] undriven_65;

  Clock u_CLK (.out(clk));
  not not_1 (not_1_out, q3);
  not not_2 (na, a);
  not not_3 (nb, b);
  not not_4 (not_4_out, q2);
  not not_5 (not_5_out, q1);
  not not_6 (not_6_out, q0);
  and and_1 (s0, undriven_9, undriven_25, undriven_41, undriven_57);
  and and_2 (s1, undriven_10, undriven_26, undriven_42, undriven_49);
  and and_3 (s2, undriven_11, undriven_27, undriven_33, undriven_58);
  and and_4 (s3, undriven_12, undriven_28, undriven_34, undriven_50);
  and and_5 (s4, undriven_13, undriven_17, undriven_43, undriven_59);
  and and_6 (s5, undriven_14, undriven_18, undriven_44, undriven_51);
  and and_7 (s6, undriven_15, undriven_19, undriven_35, undriven_60);
  and and_8 (s7, undriven_16, undriven_20, undriven_36, undriven_52);
  and and_9 (s8, undriven, undriven_29, undriven_45, undriven_61);
  and and_10 (s9, undriven_2, undriven_30, undriven_46, undriven_53);
  and and_11 (s10, undriven_3, undriven_31, undriven_37, undriven_62);
  and and_12 (s11, undriven_4, undriven_32, undriven_38, undriven_54);
  and and_13 (s12, undriven_5, undriven_21, undriven_47, undriven_63);
  and and_14 (s13, undriven_6, undriven_22, undriven_48, undriven_55);
  and and_15 (s14, undriven_7, undriven_23, undriven_39, undriven_64);
  and and_16 (s15, undriven_8, undriven_24, undriven_40, undriven_56);
  and and_17 (r1, s14, na);
  and and_18 (r2, s14, a);
  and and_19 (r3, s7, nb);
  and and_20 (r4, s7, b);
  and and_21 (r5, s0, nb);
  and and_22 (r6, s0, b);
  or or_1 (n0, r1, s8, s6, s4, s15, r5, r6, s12, s1);
  or or_2 (n1, s2, r1, s8, r3, s13, r5, r6, s3, s11, s9);
  or or_3 (n2, s2, r1, s8, r3, r4, s6, s4, s10, s15);
  or or_4 (n3, s2, r1, r2, s6, s4, s13, s10, r5, s3, s11, s1);
  D_Flip_Flop d_ff_1 (.clk(n0), .D(clk), .Q(q0));  // open: Qn, preset, en, reset
  D_Flip_Flop d_ff_2 (.clk(n1), .D(clk), .Q(q1));  // open: Qn, preset, en, reset
  D_Flip_Flop d_ff_3 (.clk(n2), .D(clk), .Q(q2));  // open: Qn, preset, en, reset
  D_Flip_Flop d_ff_4 (.clk(n3), .D(clk), .Q(q3));  // open: Qn, preset, en, reset
  Hex_Digit_Display hex_digit_display_1 (.value({undriven_65, q3}));  // open: dp

  // Notes on the sheet:
  //   Входы: CLK - тактовый сигнал, a и b - условия ветвления графа
  //   Дешифратор состояний: s0 ... s15 (код q3 q2 q1 q0)
  //   Схемы коррекции ветвления R1 ... R6
  //   Новое состояние бита 0 (newQ0)
  //   Новое состояние бита 1 (newQ1)
  //   Новое состояние бита 2 (newQ2)
  //   Новое состояние бита 3 (newQ3)
  //   D-триггер q0
  //   D-триггер q1
  //   D-триггер q2
  //   D-триггер q3
  //   Текущее состояние (hex)
endmodule
