// Logisim project INPR<-IR+MAR.circ as structural Verilog: 1 circuit, main circuit Учебное ОУ
module \Учебное_ОУ  (
  input  C,
  input  [7:0] \Ввод ,
  input  [2:0] MS_A,
  input  [2:0] MS_B,
  input  F,
  input  M,
  input  S2,
  input  S1,
  input  S0,
  input  C0,
  input  E,
  input  [2:0] x2_x1_x0,
  input  MSM_a0,
  input  WR,
  input  [7:0] \ОЗУ_DO ,
  output [7:0] \операнд_A ,
  output [7:0] \операнд_B ,
  output [7:0] \S_шина 
);

  wire en1, en2, en3, en4, en5, en6, en7, nC0;
  wire [4:2] alusel;
  wire [7:0] Mmux, q_AC, q_InpR, q_IR, q_MAR, q_MDR, q_OutR, q_PC, r_add, r_and, r_dec, r_inc, r_nand, r_nor,
       r_not, r_or, r_rol, r_ror, r_rsub, r_shl, r_shr, r_sub, r_xnor, r_xor;

  Adder #(.width(8)) adder_1 (.a(\операнд_A ), .b(\операнд_B ), .out(r_add), .cin(C0));  // open: cout
  Shifter #(.width(8), .shift("rr")) shifter_1 (.in(\операнд_A ), .\dist (3'b001), .out(r_ror));
  not not_1 (nC0, C0);
  Adder #(.width(8)) adder_2 (.a(\операнд_A ), .b({8{1'b0}}), .out(r_inc), .cin(C0));  // open: cout
  assign r_or = \операнд_A  | \операнд_B ;  // OR_Gate or_1, 8 bits wide
  Decoder #(.select(3), .enable("true")) decoder_1 (
    .out1(en1), .out2(en2), .out3(en3), .out4(en4), .out5(en5), .out6(en6), .out7(en7), .sel(x2_x1_x0), .en(E));  // open: out0
  Subtractor #(.width(8)) subtractor_1 (.a(\операнд_A ), .b(\операнд_B ), .out(r_sub), .bin(nC0));  // open: bout
  assign r_xor = \операнд_A  ^ \операнд_B ;  // XOR_Gate xor_1, 8 bits wide
  Subtractor #(.width(8)) subtractor_2 (.a(\операнд_A ), .b({8{1'b0}}), .out(r_dec), .bin(nC0));  // open: bout
  assign r_and = \операнд_A  & \операнд_B ;  // AND_Gate and_1, 8 bits wide
  Register #(.width(8)) OutR (.D(\S_шина ), .en(en1), .Q(q_OutR), .clk(C));  // open: clr
  Register #(.width(8)) InpR (.D(\S_шина ), .en(en2), .Q(q_InpR), .clk(C));  // open: clr
  Register #(.width(8)) MDR (.D(Mmux), .en(en3), .Q(q_MDR), .clk(C));  // open: clr
  Register #(.width(8)) MAR (.D(\S_шина ), .en(en4), .Q(q_MAR), .clk(C));  // open: clr
  Register #(.width(8)) IR (.D(\S_шина ), .en(en5), .Q(q_IR), .clk(C));  // open: clr
  Register #(.width(8)) AC (.D(\S_шина ), .en(en6), .Q(q_AC), .clk(C));  // open: clr
  Register #(.width(8)) PC (.D(\S_шина ), .en(en7), .Q(q_PC), .clk(C));  // open: clr
  Subtractor #(.width(8)) subtractor_3 (.a(\операнд_B ), .b(\операнд_A ), .out(r_rsub), .bin(C0));  // open: bout
  assign r_not = ~\операнд_A ;  // NOT_Gate not_2, 8 bits wide
  Shifter #(.width(8), .shift("ll")) shifter_2 (.in(\операнд_A ), .\dist (3'b001), .out(r_shl));
  assign r_nand = ~r_and;  // NOT_Gate not_3, 8 bits wide
  Multiplexer #(.select(3), .width(8), .enable("false")) multiplexer_1 (
    .in0(\Ввод ), .in1(q_OutR), .in2(q_InpR), .in3(q_MDR), .in4(q_MAR), .in5(q_IR), .in6(q_AC), .in7(q_PC),
    .out(\операнд_A ), .sel(MS_A));
  Multiplexer #(.select(3), .width(8), .enable("false")) multiplexer_2 (
    .in0(\Ввод ), .in1(q_OutR), .in2(q_InpR), .in3(q_MDR), .in4(q_MAR), .in5(q_IR), .in6(q_AC), .in7(q_PC),
    .out(\операнд_B ), .sel(MS_B));
  Shifter #(.width(8), .shift("lr")) shifter_3 (.in(\операнд_A ), .\dist (3'b001), .out(r_shr));
  assign r_nor = ~r_or;  // NOT_Gate not_4, 8 bits wide
  Shifter #(.width(8), .shift("rl")) shifter_4 (.in(\операнд_A ), .\dist (3'b001), .out(r_rol));
  assign r_xnor = ~r_xor;  // NOT_Gate not_5, 8 bits wide
  Multiplexer #(.select(1), .width(8), .enable("false")) multiplexer_3 (
    .in0(\S_шина ), .in1(\ОЗУ_DO ), .out(Mmux), .sel(MSM_a0));
  Multiplexer #(.select(5), .width(8), .enable("false")) multiplexer_4 (
    .in0(r_inc), .in1(r_add), .in2(r_sub), .in3(r_dec), .in4(r_rsub), .in5({8{1'b0}}), .in6(r_shl),
    .in7(r_shr), .in8(r_or), .in9(r_xor), .in10(r_and), .in11(r_not), .in12(r_shl), .in13(r_shr),
    .in14(r_rol), .in15(r_ror), .in16({8{1'b0}}), .in17({8{1'b0}}), .in18({8{1'b0}}), .in19({8{1'b0}}),
    .in20({8{1'b0}}), .in21({8{1'b0}}), .in22({8{1'b0}}), .in23({8{1'b0}}), .in24(r_nand), .in25(r_nor),
    .in26(r_xnor), .in27({8{1'b0}}), .in28(r_rol), .in29(r_ror), .in30({8{1'b0}}), .in31({8{1'b0}}),
    .out(\S_шина ), .sel({alusel, F, M}));

  // Other names for the same wires on the sheet: A[7:0] = \операнд_A ; a0 = MSM_a0; alusel[1:0] = {F, M};
  //   B[7:0] = \операнд_B ; DO[7:0] = \ОЗУ_DO ; msa[2:0] = MS_A; msb[2:0] = MS_B; S[7:0] = \S_шина ;
  //   VVOD[7:0] = \Ввод ; x[2:0] = x2_x1_x0

  // Notes on the sheet:
  //   УПРАВЛЯЮЩЕЕ СЛОВО
  //   АЛУ (таблица 3.1): результаты всех микроопераций
  //   A + B + C0
  //   ROR A
  //   A + C0
  //   A или B
  //   код АЛУ
  //   не C0
  //   константы
  //   ДС (запись)
  //   A - B - не C0
  //   A xor B
  //   A - не C0
  //   A и B
  //   УЧЕБНОЕ ОПЕРАЦИОННОЕ УСТРОЙСТВО (ОУ) ЦП
  //   РЕГИСТРЫ
  //   код 001
  //   код 010
  //   код 011
  //   код 100
  //   код 101
  //   код 110
  //   код 111
  //   B - A - C0
  //   не A
  //   A << 1
  //   не (A и B)
  //   MS A
  //   MS B
  //   A >> 1
  //   не (A или B)
  //   ROL A
  //   не (A xor B)
  //   MS M
  //   выбор результата АЛУ
endmodule
